// Logisim project filter.circ as structural Verilog: 1 circuit, main circuit main
module main (
);

  wire clock_1_out, clock_2_out, clock_3_out;
  wire [15:0] counter_1_q, counter_2_q, counter_3_q, counter_4_q, ram_1_data, ram_2_data, ram_3_data;

  Clock clock_1 (.out(clock_1_out));
  Counter #(.width(16), .max('h300)) counter_1 (
    .load(1'b0), .count(1'b1), .Q(counter_1_q), .clk(clock_1_out));  // open: D, carry, clr
  Counter #(.width(16), .max('h6), .ongoal("stay")) counter_2 (
    .load(1'b0), .count(1'b1), .Q(counter_2_q), .clk(clock_2_out));  // open: D, carry, clr
  Clock clock_2 (.out(clock_2_out));
  RAM #(.addrWidth(16), .dataWidth(16)) ram_1 (
    .addr(counter_1_q), .data(ram_1_data), .sel(1'b1), .clk(clock_1_out), .ld(1'b1), .clr(1'b0));
  RAM #(.addrWidth(16), .dataWidth(16)) ram_2 (
    .addr(counter_2_q), .data(ram_2_data), .sel(1'b1), .clk(clock_2_out), .ld(1'b1), .clr(1'b0));
  Clock clock_3 (.out(clock_3_out));
  Counter #(.width(16), .max('h6), .ongoal("stay")) counter_3 (
    .load(1'b0), .count(1'b1), .Q(counter_3_q), .clk(clock_3_out));  // open: D, carry, clr
  RAM #(.addrWidth(16), .dataWidth(16)) ram_3 (
    .addr(counter_3_q), .data(ram_3_data), .sel(1'b1), .clk(clock_3_out), .ld(1'b1), .clr(1'b0));
  Register #(.width(16)) register_1 (.D(ram_2_data), .en(ram_3_data[0]), .clk(clock_3_out));  // open: Q, clr
  Counter #(.width(16), .max('h300)) counter_4 (
    .load(1'b0), .count(1'b1), .Q(counter_4_q), .clk(clock_1_out));  // open: D, carry, clr
  Register #(.width(16)) register_2 (.D(ram_2_data), .en(ram_3_data[1]), .clk(clock_3_out));  // open: Q, clr
  RAM #(.addrWidth(16), .dataWidth(16)) ram_4 (
    .addr(counter_4_q), .data(ram_1_data), .sel(1'b1), .clk(clock_1_out), .ld(1'b0), .clr(1'b0));

  // Notes on the sheet:
  //   RAM que contem os dados de entrada do sistema
  //   para gerar vetor imagem, usar função no matlab 'vector2logsim'
  //   RAM que contem os dados de saída do sistema
  //   para ler a imagem, usar função no matlab 'logisim2vector'
endmodule
